// Logisim project 3.circ as structural Verilog: 1 circuit, main circuit main
module main (
);

  wire A, and_1_out, and_2_out, and_3_out, and_4_out, and_5_out, and_6_out, and_8_out, and_9_out, and_11_out,
       B, C, clock_1_out, D, E, F, go, Reset_out, t_ff_1_q, t_ff_2_q, t_ff_3_q, t_ff_4_q, t_ff_5_q, t_ff_6_q,
       X0, X1, X2, xor_1_out, xor_2_out, xor_3_out, xor_4_out, xor_5_out, xor_6_out, xor_7_out, xor_8_out,
       xor_10_out;

  // Probe on {A, B, C, D, E, F}
  // Probe on {X2, X1, X0}
  xor xor_1 (xor_1_out, A, B);
  and and_1 (and_1_out, A, B, B);
  TTY #(.rows(1), .cols(65)) tty_1 (.data({4'b0110, X2, X1, X0}), .clk(clock_1_out), .we(go), .clr(Reset_out));
  T_Flip_Flop t_ff_1 (.clk(clock_1_out), .T(1'b1), .Q(t_ff_1_q), .Qn(F), .preset(Reset_out), .en(go));  // open: reset
  Clock clock_1 (.out(clock_1_out));
  T_Flip_Flop t_ff_2 (.clk(t_ff_1_q), .T(1'b1), .Q(t_ff_2_q), .Qn(E), .preset(Reset_out));  // open: reset, en
  xor xor_2 (xor_2_out, xor_1_out, C);
  and and_2 (and_2_out, xor_1_out, C);
  T_Flip_Flop t_ff_3 (.clk(t_ff_2_q), .T(1'b1), .Q(t_ff_3_q), .Qn(D), .preset(Reset_out));  // open: reset, en
  T_Flip_Flop t_ff_4 (.clk(t_ff_3_q), .T(1'b1), .Q(t_ff_4_q), .Qn(C), .preset(Reset_out));  // open: reset, en
  xor xor_3 (xor_3_out, and_1_out, and_2_out);
  and and_3 (and_3_out, and_1_out, and_2_out);
  T_Flip_Flop t_ff_5 (.clk(t_ff_4_q), .T(1'b1), .Q(t_ff_5_q), .Qn(B), .preset(Reset_out));  // open: reset, en
  xor xor_4 (xor_4_out, xor_2_out, D);
  and and_4 (and_4_out, xor_2_out, D);
  T_Flip_Flop t_ff_6 (.clk(t_ff_5_q), .T(1'b1), .Q(t_ff_6_q), .Qn(A), .preset(Reset_out));  // open: reset, en
  xor xor_5 (xor_5_out, xor_3_out, and_4_out);
  and and_5 (and_5_out, xor_3_out, and_4_out);
  Button Reset (.out(Reset_out));
  T_Flip_Flop t_ff_7 (.clk(t_ff_6_q), .T(1'b1), .Q(go), .preset(Reset_out));  // open: Qn, reset, en
  xor xor_6 (xor_6_out, xor_4_out, E);
  and and_6 (and_6_out, xor_4_out, E);
  xor xor_7 (xor_7_out, and_3_out, and_5_out);
  // AND_Gate and_7 has open pins: in1=and_3_out, in3=and_5_out, out=open
  xor xor_8 (xor_8_out, xor_5_out, and_6_out);
  and and_8 (and_8_out, xor_5_out, and_6_out);
  xor xor_9 (X0, xor_6_out, F);
  and and_9 (and_9_out, xor_6_out, F);
  xor xor_10 (xor_10_out, xor_7_out, and_8_out);
  // AND_Gate and_10 has open pins: in1=xor_7_out, in3=and_8_out, out=open
  xor xor_11 (X1, xor_8_out, and_9_out);
  and and_11 (and_11_out, xor_8_out, and_9_out);
  xor xor_12 (X2, xor_10_out, and_11_out);
  // AND_Gate and_12 has open pins: in1=xor_10_out, in3=and_11_out, out=open

  // Notes on the sheet:
  //   0112122312232334122323342334344512232334233434452334344534454556
endmodule
