// Logisim project 4.circ as structural Verilog: 1 circuit, main circuit main
module main (
);

  wire A, and_2_out, and_3_out, and_4_out, and_6_out, and_7_out, B, C, clock_1_out, f, go, not_1_out,
       not_2_out, not_3_out, Reset_out, t_ff_1_q, t_ff_2_q, t_ff_3_q;

  // Probe on {A, B, C}
  T_Flip_Flop t_ff_1 (.clk(clock_1_out), .T(1'b1), .Q(t_ff_1_q), .Qn(C), .preset(Reset_out), .en(go));  // open: reset
  Clock clock_1 (.out(clock_1_out));
  not not_1 (not_1_out, A);
  not not_2 (not_2_out, B);
  not not_3 (not_3_out, C);
  // Probe on f
  T_Flip_Flop t_ff_2 (.clk(t_ff_1_q), .T(1'b1), .Q(t_ff_2_q), .Qn(B), .preset(Reset_out));  // open: reset, en
  TTY #(.rows(1), .cols(10)) tty_1 (.data({6'b011000, f}), .clk(clock_1_out), .we(go), .clr(Reset_out));
  T_Flip_Flop t_ff_3 (.clk(t_ff_2_q), .T(1'b1), .Q(t_ff_3_q), .Qn(A), .preset(Reset_out));  // open: reset, en
  Button Reset (.out(Reset_out));
  T_Flip_Flop t_ff_4 (.clk(t_ff_3_q), .T(1'b1), .Q(go), .preset(Reset_out));  // open: Qn, reset, en
  // AND_Gate and_1 has open pins: in0=not_1_out, in2=not_2_out, in4=not_3_out, out=open
  and and_2 (and_2_out, not_1_out, not_2_out, C);
  and and_3 (and_3_out, not_1_out, B, not_3_out);
  and and_4 (and_4_out, not_1_out, B, C);
  // AND_Gate and_5 has open pins: in0=A, in2=not_2_out, in4=not_3_out, out=open
  and and_6 (and_6_out, A, not_2_out, C);
  and and_7 (and_7_out, A, B, not_3_out);
  // AND_Gate and_8 has open pins: in0=A, in2=B, in4=C, out=open
  or or_1 (f, and_2_out, and_3_out, and_4_out, and_6_out, and_7_out);

  // Notes on the sheet:
  //   01110110
endmodule
