// Logisim project 5.circ as structural Verilog: 1 circuit, main circuit main
module main (
);

  wire A, and_1_out, and_2_out, and_3_out, B, C, clock_1_out, f, go, not_1_out, not_2_out, or_1_out,
       Reset_out, t_ff_1_q, t_ff_2_q, t_ff_3_q;

  Clock clock_1 (.out(clock_1_out));
  // Probe on f
  // Probe on {A, B, C}
  T_Flip_Flop t_ff_1 (.clk(clock_1_out), .T(1'b1), .Q(t_ff_1_q), .Qn(C), .preset(Reset_out), .en(go));  // open: reset
  not not_1 (not_1_out, C);
  T_Flip_Flop t_ff_2 (.clk(t_ff_1_q), .T(1'b1), .Q(t_ff_2_q), .Qn(B), .preset(Reset_out));  // open: reset, en
  or or_1 (or_1_out, B, not_1_out);
  and and_1 (and_1_out, B, not_1_out);
  TTY #(.rows(1), .cols(10)) tty_1 (.data({6'b011000, f}), .clk(clock_1_out), .we(go), .clr(Reset_out));
  T_Flip_Flop t_ff_3 (.clk(t_ff_2_q), .T(1'b1), .Q(t_ff_3_q), .Qn(A), .preset(Reset_out));  // open: reset, en
  not not_2 (not_2_out, A);
  Button Reset (.out(Reset_out));
  T_Flip_Flop t_ff_4 (.clk(t_ff_3_q), .T(1'b1), .Q(go), .preset(Reset_out));  // open: Qn, reset, en
  and and_2 (and_2_out, or_1_out, not_2_out);
  and and_3 (and_3_out, A, and_1_out);
  or or_2 (f, and_2_out, and_3_out);

  // Notes on the sheet:
  //   10110010
  //   2-to-1 Multiplexer
endmodule
