// Logisim project 6.circ as structural Verilog: 1 circuit, main circuit main
module main (
);

  wire a, and_1_out, and_2_out, and_3_out, and_4_out, and_5_out, and_6_out, and_7_out, and_8_out, and_9_out,
       and_10_out, and_11_out, and_12_out, and_13_out, and_14_out, and_15_out, and_16_out, and_17_out,
       and_18_out, and_19_out, and_20_out, and_21_out, and_22_out, and_23_out, b, c, clock_1_out, d, e, f, g,
       not_1_out, not_3_out, not_5_out, not_6_out, not_7_out, not_10_out, not_13_out, not_14_out, not_15_out,
       not_17_out, not_19_out, not_21_out, not_22_out, not_25_out, not_26_out, not_27_out, not_29_out,
       Reset_out, stop, w0, w1, w2, w3;

  not not_1 (not_1_out, w0);
  // NOT_Gate not_2 has open pins: in=w1, out=open
  not not_3 (not_3_out, w2);
  // NOT_Gate not_4 has open pins: in=w3, out=open
  not not_5 (not_5_out, w0);
  not not_6 (not_6_out, w1);
  not not_7 (not_7_out, w2);
  // NOT_Gate not_8 has open pins: in=w3, out=open
  // NOT_Gate not_9 has open pins: in=w0, out=open
  not not_10 (not_10_out, w1);
  // NOT_Gate not_11 has open pins: in=w2, out=open
  // NOT_Gate not_12 has open pins: in=w3, out=open
  not not_13 (not_13_out, w0);
  not not_14 (not_14_out, w1);
  not not_15 (not_15_out, w2);
  // NOT_Gate not_16 has open pins: in=w3, out=open
  not not_17 (not_17_out, w0);
  // NOT_Gate not_18 has open pins: in=w1, out=open
  not not_19 (not_19_out, w2);
  // NOT_Gate not_20 has open pins: in=w3, out=open
  not not_21 (not_21_out, w0);
  not not_22 (not_22_out, w1);
  // NOT_Gate not_23 has open pins: in=w2, out=open
  // NOT_Gate not_24 has open pins: in=w3, out=open
  not not_25 (not_25_out, w0);
  not not_26 (not_26_out, w1);
  not not_27 (not_27_out, w2);
  // NOT_Gate not_28 has open pins: in=w3, out=open
  and and_1 (and_1_out, not_1_out, not_3_out);
  buf and_2 (and_2_out, w1);  // AND_Gate
  buf and_3 (and_3_out, w3);  // AND_Gate
  and and_4 (and_4_out, w0, w2);
  and and_5 (and_5_out, not_5_out, not_6_out);
  buf and_6 (and_6_out, not_7_out);  // AND_Gate
  and and_7 (and_7_out, w0, w1);
  and and_8 (and_8_out, not_13_out, not_15_out);
  and and_9 (and_9_out, w1, not_15_out);
  and and_10 (and_10_out, not_13_out, w1);
  buf and_11 (and_11_out, w3);  // AND_Gate
  and and_12 (and_12_out, w0, not_14_out, w2);
  and and_13 (and_13_out, not_17_out, not_19_out);
  and and_14 (and_14_out, not_17_out, w1);
  and and_15 (and_15_out, not_21_out, not_22_out);
  buf and_16 (and_16_out, w3);  // AND_Gate
  and and_17 (and_17_out, not_21_out, w2);
  and and_18 (and_18_out, not_22_out, w2);
  and and_19 (and_19_out, w1, not_27_out);
  and and_20 (and_20_out, not_25_out, w1);
  buf and_21 (and_21_out, w3);  // AND_Gate
  and and_22 (and_22_out, not_26_out, w2);
  or or_1 (a, and_1_out, and_2_out, and_3_out, and_4_out);
  or or_2 (b, and_5_out, and_6_out, and_7_out);
  or or_3 (c, not_10_out, w0, w2);
  or or_4 (d, and_8_out, and_9_out, and_10_out, and_11_out, and_12_out);
  or or_5 (e, and_13_out, and_14_out);
  or or_6 (f, and_15_out, and_16_out, and_17_out, and_18_out);
  or or_7 (g, and_19_out, and_20_out, and_21_out, and_22_out);
  _7_Segment_Display u_7_segment_display_1 (.g(g), .f(f), .a(a), .b(b), .e(e), .d(d), .c(c));  // open: dp
  Clock clock_1 (.out(clock_1_out));
  // Probe on {w3, w2, w1, w0}
  and and_23 (and_23_out, clock_1_out, not_29_out);
  not not_29 (not_29_out, stop);
  TTY #(.rows(10), .cols(1)) tty_1 (.data({3'b100, d, c, b, a}), .clk(and_23_out), .clr(Reset_out));  // open: we
  Counter #(.width(4), .max('h9), .ongoal("stay")) counter_1 (
    .Q({w3, w2, w1, w0}), .carry(stop), .clk(and_23_out), .clr(Reset_out));  // open: load, D, count
  TTY #(.rows(10), .cols(1)) tty_2 (.data({4'b0110, g, f, e}), .clk(and_23_out), .clr(Reset_out));  // open: we
  Button Reset (.out(Reset_out));

  // Notes on the sheet:
  //   O
  //   F
  //   K
  //   O
  //   F
  //   M
  //   M
  //   G
  //   O
  //   3
  //   0
  //   5
  //   4
  //   6
  //   6
  //   7
  //   0
  //   7
endmodule
