// Logisim project 7.circ as structural Verilog: 1 circuit, main circuit main
module main (
);

  wire _3_out, _5_out, _6_out, _7_out, _9_out, _10_out, _11_out, _12_out, A0, A1, A2, C0, C1, C2, C3,
       clock_1_out, D0, D1, D2, D3, D4, D5, D6, D7, go, not_1_out, not_2_out, not_3_out, not_4_out,
       odd_parity_1_out, odd_parity_2_out, odd_parity_3_out, odd_parity_4_out, P0, P1, P2, Reset_out,
       t_ff_1_q, t_ff_2_q, t_ff_3_q, t_ff_4_q, t_ff_5_q, t_ff_6_q, Z0, Z1, Z2, Z3, Z4, Z5, Z6, Z7;
  wire [0:0] multiplexer_1_out;

  Clock clock_1 (.out(clock_1_out));
  T_Flip_Flop t_ff_1 (.clk(clock_1_out), .T(1'b1), .Q(t_ff_1_q), .Qn(P0), .preset(Reset_out), .en(go));  // open: reset
  Multiplexer #(.select(3), .disabled(0), .enable("false")) multiplexer_1 (
    .in0(Z7), .in1(Z6), .in2(Z5), .in3(Z4), .in4(Z3), .in5(Z2), .in6(Z1), .in7(Z0),
    .out(multiplexer_1_out[0]), .sel({P2, P1, P0}));
  T_Flip_Flop t_ff_2 (.clk(t_ff_1_q), .T(1'b1), .Q(t_ff_2_q), .Qn(P1), .preset(Reset_out));  // open: reset, en
  T_Flip_Flop t_ff_3 (.clk(t_ff_2_q), .T(1'b1), .Q(t_ff_3_q), .Qn(P2), .preset(Reset_out));  // open: reset, en
  ROM #(.addrWidth(3), .dataWidth(12)) rom_1 (
    .addr({A2, A1, A0}), .data({D7, D6, D5, D4, C3, D3, D2, D1, C2, D0, C1, C0}));  // open: sel
  TTY #(.cols(8)) tty_1 (.data({6'b011000, multiplexer_1_out[0]}), .clk(clock_1_out), .we(go), .clr(Reset_out));
  T_Flip_Flop t_ff_4 (.clk(t_ff_3_q), .T(1'b1), .Q(t_ff_4_q), .Qn(A0), .preset(Reset_out));  // open: reset, en
  // Probe on {D7, D6, D5, D4, C3, D3, D2, D1, C2, D0, C1, C0}
  xor odd_parity_1 (odd_parity_1_out, C0, D0, D1, D3, D4, D6);
  xor odd_parity_2 (odd_parity_2_out, C1, D0, D2, D3, D5, D6);
  xor odd_parity_3 (odd_parity_3_out, C2, D1, D2, D3, D7);
  xor odd_parity_4 (odd_parity_4_out, C3, D4, D5, D6, D7);
  T_Flip_Flop t_ff_5 (.clk(t_ff_4_q), .T(1'b1), .Q(t_ff_5_q), .Qn(A1), .preset(Reset_out));  // open: reset, en
  not not_1 (not_1_out, odd_parity_1_out);
  not not_2 (not_2_out, odd_parity_2_out);
  not not_3 (not_3_out, odd_parity_3_out);
  not not_4 (not_4_out, odd_parity_4_out);
  T_Flip_Flop t_ff_6 (.clk(t_ff_5_q), .T(1'b1), .Q(t_ff_6_q), .Qn(A2), .preset(Reset_out));  // open: reset, en
  Button Reset (.out(Reset_out));
  T_Flip_Flop t_ff_7 (.clk(t_ff_6_q), .T(1'b1), .Q(go), .preset(Reset_out));  // open: Qn, reset, en
  and _3 (_3_out, odd_parity_1_out, odd_parity_2_out, not_3_out, not_4_out);
  and _5 (_5_out, odd_parity_1_out, not_2_out, odd_parity_3_out, not_4_out);
  and _6 (_6_out, not_1_out, odd_parity_2_out, odd_parity_3_out, not_4_out);
  and _7 (_7_out, odd_parity_1_out, odd_parity_2_out, odd_parity_3_out, not_4_out);
  and _9 (_9_out, odd_parity_1_out, not_2_out, not_3_out, odd_parity_4_out);
  and _10 (_10_out, not_1_out, odd_parity_2_out, not_3_out, odd_parity_4_out);
  and _11 (_11_out, odd_parity_1_out, odd_parity_2_out, not_3_out, odd_parity_4_out);
  and _12 (_12_out, not_1_out, not_2_out, odd_parity_3_out, odd_parity_4_out);
  xor xor_1 (Z0, D0, _3_out);
  xor xor_2 (Z1, D1, _5_out);
  xor xor_3 (Z2, D2, _6_out);
  xor xor_4 (Z3, D3, _7_out);
  xor xor_5 (Z4, D4, _9_out);
  xor xor_6 (Z5, D5, _10_out);
  xor xor_7 (Z6, D6, _11_out);
  xor xor_8 (Z7, D7, _12_out);

  // Notes on the sheet:
  //   contents of rom_1 (hex, n*v repeats v):
  //   d7 788 a75 a74 275 b75 f75 a77
  //   Find Error Bit
  //   00101011
  //   01110000
  //   10101111
  //   10101111
  //   10101111
  //   10101111
  //   11111111
  //   10101111
  //   Locate Bit
  //   Error Correction
endmodule
