// Logisim project 1.circ as structural Verilog: 1 circuit, main circuit main
module main (
);

  wire _15, _30, CLOCK, clock_1_out, counter_2_carry, d_ff_1_qn, d_ff_2_qn, not_1_out, Reset_out;
  wire [7:0] counter_1_q, counter_3_q;

  D_Flip_Flop d_ff_1 (.clk(CLOCK), .D(d_ff_1_qn), .Q(_30), .Qn(d_ff_1_qn));  // open: preset, en, reset
  D_Flip_Flop d_ff_2 (.clk(_30), .D(d_ff_2_qn), .Q(_15), .Qn(d_ff_2_qn));  // open: preset, en, reset
  // Probe on counter_1_q
  Counter counter_1 (.Q(counter_1_q), .clk(_30));  // open: load, D, count, carry, clr
  Counter counter_2 (.carry(counter_2_carry), .clk(CLOCK), .clr(Reset_out));  // open: load, D, count, Q
  and and_1 (CLOCK, clock_1_out, not_1_out);
  Clock clock_1 (.out(clock_1_out));
  // Probe on counter_3_q
  Counter counter_3 (.Q(counter_3_q), .clk(_15));  // open: load, D, count, carry, clr
  not not_1 (not_1_out, counter_2_carry);
  Button Reset (.out(Reset_out));

  // Notes on the sheet:
  //   1 0 0 0 00 0 0
  //   0 1 0 0 0 0 0 0
endmodule
