// Logisim project 6.circ as structural Verilog: 1 circuit, main circuit main
module main (
);

  wire _4_Counter_carry, A, A_prime_B_out, A_prime_B_prime_D_out, A_prime_BD_prime_out, A_prime_CD_out,
       AB_prime_C_out, AB_prime_out, ABC_prime_D_out, B, C, CLK, clock_1_out, go, nA, nB, nC, not_1_out,
       not_2_out, not_3_out, or_1_out, or_2_out, Q, Reset_out, w;
  wire [1:0] _4_Counter_q;
  wire [4:0] _32_Counter_q;

  not not_1 (not_1_out, w);
  and A_prime_B (A_prime_B_out, nA, B);
  and AB_prime (AB_prime_out, A, nB);
  and A_prime_B_prime_D (A_prime_B_prime_D_out, nA, nB, w);
  and A_prime_CD (A_prime_CD_out, nA, C, w);
  and A_prime_BD_prime (A_prime_BD_prime_out, nA, B, not_1_out);
  and AB_prime_C (AB_prime_C_out, A, nB, C);
  and ABC_prime_D (ABC_prime_D_out, A, B, nC, w);
  or or_1 (or_1_out, A_prime_B_out, AB_prime_out);
  or or_2 (or_2_out, A_prime_B_prime_D_out, A_prime_CD_out, A_prime_BD_prime_out, AB_prime_C_out, ABC_prime_D_out);
  not not_2 (not_2_out, or_1_out);
  not not_3 (not_3_out, nB);
  TTY #(.rows(17), .cols(4)) tty_1 (.data({6'b011000, Q}), .clk(CLK), .we(go), .clr(Reset_out));
  D_Flip_Flop d_ff_1 (.clk(CLK), .D(or_1_out), .Q(A), .Qn(nA));  // open: preset, en, reset
  D_Flip_Flop d_ff_2 (.clk(CLK), .D(nB), .Q(B), .Qn(nB));  // open: preset, en, reset
  D_Flip_Flop d_ff_3 (.clk(CLK), .D(or_2_out), .Q(C), .Qn(nC));  // open: preset, en, reset
  Button Reset (.out(Reset_out));
  and and_1 (Q, not_2_out, not_3_out, or_2_out);
  and and_2 (CLK, clock_1_out, go);
  Clock clock_1 (.out(clock_1_out));
  // Probe on _4_Counter_q
  Counter #(.width(2), .max('h3)) _4_Counter (
    .Q(_4_Counter_q), .carry(_4_Counter_carry), .clk(CLK), .clr(Reset_out));  // open: load, D, count
  // Probe on _32_Counter_q[3:0]
  Counter #(.width(5), .max('h1f), .trigger("falling")) _32_Counter (
    .Q(_32_Counter_q), .clk(_4_Counter_carry), .clr(Reset_out));  // open: load, D, count, carry
  // Probe on w
  BitSelector #(.width(4)) bitselector_1 (.in(_32_Counter_q[3:0]), .out(w), .sel(_4_Counter_q));
  not not_4 (go, _32_Counter_q[4]);

  // Notes on the sheet:
  //   13 gates
  //   0000
  //   1000
  //   0100
  //   1100
  //   0010
  //   1010
  //   0110
  //   1110
  //   0001
  //   1001
  //   0101
  //   1101
  //   0011
  //   1011
  //   0111
  //   1111
  //   1
  //   1
endmodule
