// Logisim project 7.circ as structural Verilog: 1 circuit, main circuit main
module main (
);

  wire _5_Counter_carry, A, A_prime, AD_prime_E_out, and_1_out, and_2_out, and_3_out, and_4_out, and_5_out,
       and_6_out, and_7_out, and_8_out, and_9_out, and_10_out, B, B_prime, BC_prime_E_prime_out,
       BD_prime_E_out, C, C_prime, CD_prime_E_out, CLK, clock_1_out, D, D_prime, go, not_1_out, or_1_out,
       or_2_out, or_3_out, or_4_out, p, Reset_out, w;
  wire [2:0] _5_Counter_q;
  wire [5:0] _64_Counter_q;

  not not_1 (not_1_out, w);
  and and_1 (and_1_out, B, C, not_1_out);
  and AD_prime_E (AD_prime_E_out, A, D_prime, w);
  and and_2 (and_2_out, B, C_prime, D, w);
  and and_3 (and_3_out, B_prime, C, not_1_out);
  and BC_prime_E_prime (BC_prime_E_prime_out, B, C_prime, not_1_out);
  and BD_prime_E (BD_prime_E_out, B, D_prime, w);
  and and_4 (and_4_out, A_prime, B_prime, D, w);
  and and_5 (and_5_out, B_prime, C, w);
  and CD_prime_E (CD_prime_E_out, C, D_prime, w);
  and and_6 (and_6_out, A, D, w);
  and and_7 (and_7_out, A_prime, B_prime, D_prime, w);
  and and_8 (and_8_out, A_prime, C_prime, D, not_1_out);
  and and_9 (and_9_out, D, not_1_out);
  and and_10 (and_10_out, A_prime, B_prime, C_prime, not_1_out);
  or or_1 (or_1_out, and_1_out, AD_prime_E_out, and_2_out);
  or or_2 (or_2_out, and_3_out, BC_prime_E_prime_out, BD_prime_E_out, and_4_out);
  or or_3 (or_3_out, and_5_out, CD_prime_E_out, BC_prime_E_prime_out, and_6_out, and_7_out, and_8_out);
  or or_4 (or_4_out, and_9_out, CD_prime_E_out, BD_prime_E_out, AD_prime_E_out, and_10_out);
  D_Flip_Flop d_ff_1 (.clk(CLK), .D(or_1_out), .Q(A), .Qn(A_prime));  // open: preset, en, reset
  D_Flip_Flop d_ff_2 (.clk(CLK), .D(or_2_out), .Q(B), .Qn(B_prime));  // open: preset, en, reset
  D_Flip_Flop d_ff_3 (.clk(CLK), .D(or_3_out), .Q(C), .Qn(C_prime));  // open: preset, en, reset
  D_Flip_Flop d_ff_4 (.clk(CLK), .D(or_4_out), .Q(D), .Qn(D_prime));  // open: preset, en, reset
  TTY #(.rows(33), .cols(5)) tty_1 (.data({6'b011000, p}), .clk(CLK), .we(go), .clr(Reset_out));
  Button Reset (.out(Reset_out));
  // Probe on w
  nand nand_1 (go, _64_Counter_q[0], _64_Counter_q[5]);
  Counter #(.width(3), .max('h4)) _5_Counter (
    .Q(_5_Counter_q), .carry(_5_Counter_carry), .clk(CLK), .clr(Reset_out));  // open: load, D, count
  and and_11 (CLK, clock_1_out, go);
  Clock clock_1 (.out(clock_1_out));
  and and_12 (p, A, B_prime, C_prime, D);
  Counter #(.width(6), .max('h3f), .trigger("falling")) _64_Counter (
    .Q(_64_Counter_q), .clk(_5_Counter_carry), .clr(Reset_out));  // open: load, D, count, carry
  // Probe on _5_Counter_q
  // Probe on _64_Counter_q
  BitSelector #(.width(6)) bitselector_1 (.in(_64_Counter_q), .out(w), .sel(_5_Counter_q));

  // Notes on the sheet:
  //   1  0
  //   1  3
  //   1  5
  //   1  6
  //   1  9
  //   1   10
  //   1  12
  //   1  15
  //   1  17
  //   1  18
  //   1  20
  //   1  23
  //   1  24
  //   1 27
  //   1  29
  //   1  30
  //   24 Gates
endmodule
