// Logisim project 8.circ as structural Verilog: 1 circuit, main circuit main
module main (
);

  wire _4_Counter_carry, _5_2_out, _5_out, _10_out, _15_2_out, _15_out, A, A_prime,
       A_prime_B_prime_E_prime_out, A_prime_C_prime_D_prime_out, B, B_prime, B_prime_CD_prime_out,
       B_prime_CE_prime_out, BC_prime_D_prime_out, BC_prime_E_out, BCD_prime_out, C, C_prime, CLK,
       clock_1_out, go, I5, I10, I25, O5, O10, OM, or_3_out, or_4_out, or_5_out, or_6_out, Reset_out, w0, w1;
  wire [4:0] _4_Counter_q;

  TTY #(.rows(1), .cols(33)) tty_1 (.data({4'b1000, OM, O10, O5}), .clk(CLK), .we(go), .clr(Reset_out));
  or or_1 (w0, I5, I25);
  or or_2 (w1, I25, I10);
  Button Reset (.out(Reset_out));
  and and_1 (CLK, clock_1_out, go);
  Clock clock_1 (.out(clock_1_out));
  and BC_prime_E (BC_prime_E_out, B, C_prime, I10);
  and BCD_prime (BCD_prime_out, B, C, I5);
  and A_prime_B_prime_E_prime (A_prime_B_prime_E_prime_out, A_prime, B_prime, I10);
  and B_prime_CD_prime (B_prime_CD_prime_out, B_prime, C, I5);
  and BC_prime_D_prime (BC_prime_D_prime_out, B, C_prime, I5);
  and A_prime_C_prime_D_prime (A_prime_C_prime_D_prime_out, A_prime, C_prime, I5);
  and B_prime_CE_prime (B_prime_CE_prime_out, B_prime, C, I10);
  // Probe on _4_Counter_q
  Counter #(.width(5), .max('h1f)) _4_Counter (
    .Q(_4_Counter_q), .carry(_4_Counter_carry), .clk(CLK), .clr(Reset_out));  // open: load, D, count
  not not_1 (go, _4_Counter_carry);
  or or_3 (or_3_out, BC_prime_E_out, BCD_prime_out);
  or or_4 (or_4_out, A_prime_B_prime_E_prime_out, B_prime_CD_prime_out, BC_prime_D_prime_out);
  or or_5 (or_5_out, A_prime_C_prime_D_prime_out, B_prime_CE_prime_out);
  // Probe on I5
  ROM #(.addrWidth(5), .dataWidth(3)) rom_1 (.addr(_4_Counter_q), .data({I25, I10, I5}));  // open: sel
  // Probe on I25
  // Probe on I10
  D_Flip_Flop d_ff_1 (.clk(CLK), .D(or_3_out), .Q(A), .Qn(A_prime));  // open: preset, en, reset
  D_Flip_Flop d_ff_2 (.clk(CLK), .D(or_4_out), .Q(B), .Qn(B_prime));  // open: preset, en, reset
  D_Flip_Flop d_ff_3 (.clk(CLK), .D(or_5_out), .Q(C), .Qn(C_prime));  // open: preset, en, reset
  or or_6 (or_6_out, or_3_out, or_4_out, or_5_out);
  not not_2 (OM, or_6_out);
  and _5 (_5_out, A_prime, B_prime, C, w1, w0);
  and _5_2 (_5_2_out, A, B_prime, C_prime, w1, I10);
  and _10 (_10_out, A_prime, B, C_prime, w1, w0);
  and _15 (_15_out, A_prime, B, C, w1, w0);
  and _15_2 (_15_2_out, A, B_prime, C_prime, w1, w0);
  or or_7 (O5, _5_out, _5_2_out, _15_out, _15_2_out);
  or or_8 (O10, _10_out, _15_out, _15_2_out);

  // Other names for the same wires on the sheet: w1_prime = I5; w0_prime = I10

  // Notes on the sheet:
  //   3 to 2 Signal
  //   24 Gates
  //   D@@@@D@@@D@@E@E@F@@G@@G@F@@E@@@
  //   Deposit Check
  //   5
  //   001 11
  //   100 10
  //   contents of rom_1 (hex, n*v repeats v):
  //   4 6*1 2 1 1 2 2 2 1 4 2 4 2 2 4 1 2 4 2 4 2 2 2 1 1 1 2
  //   Change Return
  //   ABC w1w0
  //   10
  //   15
  //   011 11
  //   010 11
  //   100 11
endmodule
