// Logisim project alu.circ as structural Verilog: 1 circuit, main circuit main
module main (
);

  wire _00C0, _00C1, _00C2, _00C3, _00C4, _01C0, _01C1, _01C2, _01C3, _01C4, _10C0, _10C1, _10C2, _10C3,
       _10C4, _11C0, _11C1, _11C2, _11C3, _11C4, A0, A1, A2, A3, A4, B0, B1, B2, B3, B4, C0, C0_2_out,
       C0_3_out, C0_4_out, C0_5_out, C0_out, C1, C1_2_out, C1_3_out, C1_4_out, C1_5_out, C1_6_out, C1_7_out,
       C1_8_out, C1_9_out, C1_10_out, C1_11_out, C1_12_out, C1_13_out, C1_14_out, C1_out, C2, C3, C4, C5,
       CIN, clock_1_out, clock_2_out, go, HCLK, not_1_out, reset, S0, S1;
  wire [2:0] multiplexer_1_out;
  wire [6:1] counter_1_q;

  // Probe on {C5, C4, C3}
  // Probe on {C2, C1, C0}
  Multiplexer #(.width(3)) multiplexer_1 (
    .in0({C5, C4, C3}), .in1({C2, C1, C0}), .out(multiplexer_1_out), .sel(HCLK));  // open: en
  // Probe on multiplexer_1_out
  // Probe on {4'b0110, multiplexer_1_out}
  TTY #(.rows(32), .cols(2)) tty_1 (.data({4'b0110, multiplexer_1_out}), .clk(clock_1_out), .we(go), .clr(reset));
  Clock clock_1 (.out(clock_1_out));
  Multiplexer #(.select(2)) multiplexer_2 (
    .in0(_00C0), .in1(_01C0), .in2(_10C0), .in3(_11C0), .out(C0), .sel({S1, S0}));  // open: en
  Multiplexer #(.select(2)) multiplexer_3 (
    .in0(_00C1), .in1(_01C1), .in2(_10C1), .in3(_11C1), .out(C1), .sel({S1, S0}));  // open: en
  Multiplexer #(.select(2)) multiplexer_4 (
    .in0(_00C2), .in1(_01C2), .in2(_10C2), .in3(_11C2), .out(C2), .sel({S1, S0}));  // open: en
  Multiplexer #(.select(2)) multiplexer_5 (
    .in0(_00C3), .in1(_01C3), .in2(_10C3), .in3(_11C3), .out(C3), .sel({S1, S0}));  // open: en
  Multiplexer #(.select(2)) multiplexer_6 (
    .in0(_00C4), .in1(_01C4), .in2(_10C4), .in3(_11C4), .out(C4), .sel({S1, S0}));  // open: en
  // Probe on {A4, A3, A2, A1, A0, CIN}
  // Probe on {B4, B3, B2, B1, B0}
  // Probe on S1
  Counter #(.width(7), .max('h7f), .ongoal("stay")) counter_1 (
    .Q({counter_1_q, HCLK}), .clk(clock_2_out), .clr(reset));  // open: load, D, count, carry
  Clock clock_2 (.out(clock_2_out));
  and and_1 (_00C0, A0, B0);
  and and_2 (_00C1, A1, B1);
  and and_3 (_00C2, A2, B2);
  and and_4 (_00C3, A3, B3);
  and and_5 (_00C4, A4, B4);
  // Probe on S0
  not not_1 (not_1_out, HCLK);
  Button u_Reset (.out(reset));
  Random #(.width(13), .seed(34573)) random_1 (
    .clk(not_1_out), .next(go), .out({B4, B3, B2, B1, B0, A4, A3, A2, A1, A0, CIN, S1, S0}), .clr(reset));
  not not_2 (go, counter_1_q[6]);
  or or_1 (_01C0, A0, B0);
  or or_2 (_01C1, A1, B1);
  or or_3 (_01C2, A2, B2);
  or or_4 (_01C3, A3, B3);
  or or_5 (_01C4, A4, B4);
  not not_3 (_10C0, A0);
  not not_4 (_10C1, A1);
  not not_5 (_10C2, A2);
  not not_6 (_10C3, A3);
  not not_7 (_10C4, A4);
  xor u_C0 (C0_out, A0, B0);
  and u_C1 (C1_out, A0, B0);
  xor C0_2 (C0_2_out, A1, B1);
  and C1_2 (C1_2_out, A1, B1);
  xor C0_3 (C0_3_out, A2, B2);
  and C1_3 (C1_3_out, A2, B2);
  xor C0_4 (C0_4_out, A3, B3);
  and C1_4 (C1_4_out, A3, B3);
  xor C0_5 (C0_5_out, A4, B4);
  and C1_5 (C1_5_out, A4, B4);
  xor C0_6 (_11C0, CIN, C0_out);
  and C1_6 (C1_6_out, C0_out, CIN);
  xor C0_7 (_11C1, C1_11_out, C0_2_out);
  and C1_7 (C1_7_out, C0_2_out, C1_11_out);
  xor C0_8 (_11C2, C1_12_out, C0_3_out);
  and C1_8 (C1_8_out, C0_3_out, C1_12_out);
  xor C0_9 (_11C3, C1_13_out, C0_4_out);
  and C1_9 (C1_9_out, C0_4_out, C1_13_out);
  xor C0_10 (_11C4, C1_14_out, C0_5_out);
  and C1_10 (C1_10_out, C0_5_out, C1_14_out);
  or C1_11 (C1_11_out, C1_6_out, C1_out);
  or C1_12 (C1_12_out, C1_7_out, C1_2_out);
  or C1_13 (C1_13_out, C1_8_out, C1_3_out);
  or C1_14 (C1_14_out, C1_9_out, C1_4_out);
  or C1_15 (C5, C1_10_out, C1_5_out);

  // Notes on the sheet:
  //   SWITCH
  //   07
  //   51
  //   40
  //   51
  //   77
  //   77
  //   57
  //   63
  //   43
  //   77
  //   60
  //   51
  //   46
  //   71
  //   32
  //   43
  //   34
  //   50
  //   53
  //   00
  //   07
  //   02
  //   74
  //   04
  //   35
  //   52
  //   52
  //   50
  //   65
  //   46
  //   11
  //   57
  //   AND
  //   OR
  //   NOT
  //   ADD
endmodule
